// Logisim project LC-2200-16.circ as structural Verilog
module my_circuit (
);

  wire CLK_prime, DrPC, LdA, LdB, LdPC;
  wire [15:0] A_q, B_q, controlled_buffer_1_out, PC_q, undriven;

  Register #(.width(16)) PC (.D(undriven), .en(LdPC), .Q(PC_q), .clk(CLK_prime));  // open: clr
  assign controlled_buffer_1_out = DrPC ? PC_q : 16'bz;  // Controlled_Buffer controlled_buffer_1
  Register #(.width(16)) A (.D(undriven), .en(LdA), .Q(A_q), .clk(CLK_prime));  // open: clr
  Register #(.width(16)) B (.D(undriven), .en(LdB), .Q(B_q), .clk(CLK_prime));  // open: clr
endmodule
